# Fritzing sketch SMcounter_circuit (saved by Fritzing 0.9.4)
circuit board: 8.46667cm x 5.64444cm

parts:
  WeMos_D1_Mini1 = WeMos D1 Mini
  BPW_40 = LTR-301 [package=ltr-301]
  Diode = Rectifier Diode [part_number=1N4001 package="300 mil [THT]"]
  D2 = Rectifier Diode [part_number=1N4001 package="300 mil [THT]"]
  R1 = Resistor [tolerance=±5% resistance=10k package=THT]
  BPW_40_2 = LTR-301 [package=ltr-301]

nets:
  N1: WeMos_D1_Mini1.3V3, BPW_40.C, BPW_40_2.C
  N2: WeMos_D1_Mini1.D1, BPW_40.E, Diode.anode
  N3: WeMos_D1_Mini1.D2, D2.anode, BPW_40_2.E
  N4: WeMos_D1_Mini1.G, R1.Pin_1
  N5: Diode.cathode, D2.cathode, R1.Pin_0
